# Fritzing sketch OpenROV-mcu (saved by Fritzing 0.7.4b)
breadboards: 1

parts:
  XTAL1 = Crystal [frequency="16 Mhz" package=THT]
  C1 = Ceramic Capacitor [capacitance=22pF package="100 mil [THT, multilayer]"]
  C2 = Ceramic Capacitor [capacitance=22pF package="100 mil [THT, multilayer]"]
  U1 = atmega328 [package=dip]
  R1 = Resistor [tolerance=±5% resistance=20k package=THT]
  R2 = Resistor [tolerance=±5% resistance=10k package=THT]
  U2 = mystery part, 1 pin [chip_label="BB RX" spacing=300mil]
  U3 = mystery part, 1 pin [chip_label="BB TX" spacing=300mil]
  U4 = mystery part, 1 pin [chip_label=Servo spacing=300mil]
  U5 = mystery part, 1 pin [chip_label=Servo spacing=300mil]
  U6 = mystery part, 1 pin [chip_label=Servo spacing=300mil]
  Q1 = NPN-Transistor [package="TO92 [THT]"]
  R3 = Resistor [tolerance=±5% resistance=100k package=THT]
  R4 = Resistor [tolerance=±5% resistance=1k package=THT]
  U7 = mystery part, 1 pin [chip_label="BB GPIO" spacing=300mil]

nets:
  N1: XTAL1.pin_0, C2.1, U1.XLAT1
  N2: XTAL1.pin_1, C1.1, U1.XLAT2
  GND: C1.0, C2.0, U1.GND, R1.Pin_1, Q1.E
  N3: U1.RESET, Q1.C, R3.Pin_1
  N4: U1.D0_(RX), U3.pin1
  N5: U1.D1_(TX), R1.Pin_0, R2.Pin_0
  5V: U1.VCC, U1.AVCC, U1.AREF, R3.Pin_0
  N6: U1.D9_(PWM), U6.pin1
  N7: U1.D10_(PWM), U5.pin1
  N8: U1.D11_(PWM), U4.pin1
  N9: R2.Pin_1, U2.pin1
  N10: Q1.B, R4.Pin_0
  N11: R4.Pin_1, U7.pin1
