# Fritzing sketch OpenROV-power (saved by Fritzing 0.7.4b)
breadboards: 1

parts:
  Q1 = NPN-Transistor [package="TO92 [THT]"]
  D1 = Rectifier Diode [part_number=1N4004 package="300 mil [THT]"]
  U1 = Voltage Regulator - 5V [package="TO220 [THT]"]
  R1 = Resistor [tolerance=±5% resistance=3.3 package=THT]
  C1 = Ceramic Capacitor [capacitance=100nF package="100 mil [THT, multilayer]"]
  D2 = Rectifier Diode [part_number=1N4004 package="300 mil [THT]"]
  D3 = Rectifier Diode [part_number=1N4004 package="300 mil [THT]"]
  S1 = Pushbutton [package=THT]
  DC_Power1 = DC Power [voltage=12]

nets:
  N1: Q1.E, U1.input_voltage
  N2: Q1.B, R1.Pin_0
  N3: Q1.C, D1.cathode, D3.cathode
  9V: D1.anode
  GND: U1.GND, C1.0, DC_Power1.GND
  N4: R1.Pin_1, C1.1, D2.cathode
  N5: D2.anode, D3.anode, S1.leg0
  N6: S1.leg1, DC_Power1.V+
